# Fritzing sketch schematic (saved by Fritzing 0.9.4)

parts:
  U1 = ESP32S-HiLetgo [part_number=ESP32S-HiLetgo]
  S2 = Pushbutton [package="[THT]"]
  S3 = Pushbutton [package="[THT]"]
  S4 = Pushbutton [package="[THT]"]
  S5 = Pushbutton [package="[THT]"]
  S6 = Pushbutton [package="[THT]"]
  S7 = Pushbutton [package="[THT]"]
  S8 = Pushbutton [package="[THT]"]
  S9 = Pushbutton [package="[THT]"]
  Grove1 = Grove OLED 128x96
  Part1 = NeoPixel NeoMatrix 8x8 [part_number=1487]
  RE1 = KY-040 Rotary encoder [package=THT]
  S10 = Pushbutton [package="[THT]"]
  LED1 = LED - 5mm [color="Red (633nm)" package="5 mm [THT]"]
  R1 = Resistor [tolerance=±5% resistance=220 package=THT]

nets:
  N1: U1.3.3, RE1.Vcc
  N2: U1.GPIO36, S9.Pin_2
  N3: U1.GPIO39, S7.Pin_1, S7.Pin_2
  N4: U1.GPIO34, S6.Pin_2
  N5: U1.GPIO35, S8.Pin_1, S8.Pin_2
  N6: U1.GPIO32, S5.Pin_2
  N7: U1.GPIO25, S2.Pin_2
  N8: U1.GPIO26, S3.Pin_1, S3.Pin_2
  N9: U1.GPIO27, S4.Pin_2
  N10: U1.GPIO14, S10.Pin_1, S10.Pin_2
  GND: U1.GND, S4.Pin_3, S4.Pin_4, Grove1.GND, Part1.GND, RE1.GND, R1.Pin_0
  VIN: U1.VIN, Grove1.VCC, Part1.IN
  N11: U1.GPIO5, LED1.anode
  N12: U1.GPIO18, RE1.CLK
  N13: U1.GPIO19, RE1.DT
  N14: U1.GPIO21, Grove1.SDA
  N15: U1.GPIO22, Grove1.SCL
  N16: U1.GPIO23, Part1.VDD

notes:
  record/ˆ/ˇ/power/ok/down/up/right/left

custom parts:
  ESP32S-HiLetgo: HiLetgo ESP-WROOM-32 ESP32 ESP-32S Development Board 2.4GHz Dual-Mode WiFi + Bluetooth Dual Cores Microcontroller The ESP32 integrated with Antenna switches, RF Balun, power amplifiers, low-noise amplifiers, filters, and management modules, and the entire solution occupies the least area of PCB. 2.4 GHz Wi-Fi plus Bluetooth dual-mode chip, with TSMC Ultra-low power consumption 40nm technology,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
  NeoPixel NeoMatrix 8x8: Put on your sunglasses before wiring up this LED matrix - 64 eye-blistering RGB LEDs adorn the NeoMatrix for a blast of configurable color. Arranged in an 8x8 matrix, each pixel is individually addressable. Only one microcontroller pin is required to control all the LEDs, and you get 24 bit color for each LED.
  KY-040 Rotary encoder: KY-040 Rotary Encoder with switch on breakout borad from AZ Delivery
